# Fritzing sketch water gun (saved by Fritzing 0.9.4)

parts:
  U1 = Module 4 Relais 5V [package="Module 4 Relais 5V"]
  Part1 = Arduino Uno (Rev3)
  J1 = Basic Servo
  BAT1 = 12 battery [package=battery]  # not connected
  Buck_Convertor1 = Buck Convertor [part_number=LM2596 package=THT]
  Buck_Convertor2 = Buck Convertor [part_number=LM2596 package=THT]
  M3 = DC Motor
  M4 = DC Motor
  Mod1 = flyskyr6b

nets:
  VCC: U1.VCC, Part1.5V
  GND: U1.GND, Part1.GND
  N1: U1.IN1, Part1.D7
  N2: U1.IN2, Part1.D8
  N3: U1.IN3, Part1.D9_PWM
  N4: U1.K1-NF, M4.pin_1
  N5: U1.K2-NF, M4.pin_2
  N6: U1.K3-NF, Buck_Convertor1.Positive_Output
  N7: Part1.D10_PWM/SS, J1.pulse
  N8: Part1.D4, Mod1.CH1
  N9: Part1.D5_PWM, Mod1.CH2
  N10: Part1.D6_PWM, Mod1.CH5
  N11: Part1.VIN, Buck_Convertor1.Positive_Input
  N12: J1.gnd, Buck_Convertor2.Negative_Output
  N13: J1.vcc, Buck_Convertor2.Positive_Output
  N14: Buck_Convertor1.Negative_Output, M3.pin_1

notes:
  Motor 12v
  5RPM
  Pump 8.4v
  8.4v
  5v

custom parts:
  Module 4 Relais 5V: Module 4 Relais 5V 4x SPD-06VDC-SD-C
  12 battery: 12V lead acid type battery, like the Husqvarna YTH2448 12V 35AH battery. This is the mini version 1/4 the size of the actual battery to be closer to typical breadboard parts (around 2in wide rathher than 7in). The pads in pcb are sized to accomidate up to 14ga wire (as these batterys will deliver high currents.)
  Buck Convertor: DC to DC buck convertor
  flyskyr6b: flysky r6b 6ch rc receiver module. Pcb view is 3*7 header pins, 3 female headers will let the board plug in to the receiver, or connect via wires as you choose.
